// Logisim project ex1.circ as structural Verilog: 8 circuits, main circuit main
module main (
  input  [15:0] in_1,
  input  [3:0] in_2,
  output [15:0] out_3
);

  rotl rotl_1 (.in_1(in_1), .in_2(in_2), .out_3(out_3));
endmodule

module Ex1 (
  input  [7:0] Input,
  output [7:0] Out2,
  output Out1
);

  and and_1 (Out1, Input[0], Input[7]);

  assign Out2 = Input;
endmodule

module rotr (
  input  [15:0] in_1,
  input  [3:0] in_2,
  output [15:0] out_3
);

  wire [14:0] multiplexer_3_out;
  wire [15:0] multiplexer_1_out, multiplexer_2_out;
  wire [15:15] multiplexer_3_out_2;

  Multiplexer #(.width(16)) multiplexer_1 (
    .in0(in_1), .in1({in_1[7:0], in_1[15:8]}), .out(multiplexer_1_out), .sel(in_2[3]));  // open: en
  Multiplexer #(.width(16)) multiplexer_2 (
    .in0(multiplexer_1_out), .in1({multiplexer_1_out[3:0], multiplexer_1_out[15:4]}),
    .out(multiplexer_2_out), .sel(in_2[2]));  // open: en
  Multiplexer #(.width(16)) multiplexer_3 (
    .in0(multiplexer_2_out), .in1({multiplexer_2_out[1:0], multiplexer_2_out[15:2]}),
    .out({multiplexer_3_out, multiplexer_3_out_2[15]}), .sel(in_2[1]));  // open: en
  Multiplexer #(.width(16)) multiplexer_4 (
    .in0({multiplexer_3_out, multiplexer_3_out_2[15]}), .in1({multiplexer_3_out_2[15], multiplexer_3_out}),
    .out(out_3), .sel(in_2[0]));  // open: en
endmodule

module rotl (
  input  [15:0] in_1,
  input  [3:0] in_2,
  output [15:0] out_3
);

  wire [0:0] multiplexer_3_out;
  wire [14:0] multiplexer_3_out_2;
  wire [15:0] multiplexer_1_out, multiplexer_2_out;

  Multiplexer #(.width(16)) multiplexer_1 (
    .in0(in_1), .in1({in_1[7:0], in_1[15:8]}), .out(multiplexer_1_out), .sel(in_2[3]));  // open: en
  Multiplexer #(.width(16)) multiplexer_2 (
    .in0(multiplexer_1_out), .in1({multiplexer_1_out[11:0], multiplexer_1_out[15:12]}),
    .out(multiplexer_2_out), .sel(in_2[2]));  // open: en
  Multiplexer #(.width(16)) multiplexer_3 (
    .in0(multiplexer_2_out),
    .in1({multiplexer_2_out[15:14], multiplexer_2_out[11:0], multiplexer_2_out[13:12]}),
    .out({multiplexer_3_out[0], multiplexer_3_out_2}), .sel(in_2[1]));  // open: en
  Multiplexer #(.width(16)) multiplexer_4 (
    .in0({multiplexer_3_out[0], multiplexer_3_out_2}), .in1({multiplexer_3_out_2, multiplexer_3_out[0]}),
    .out(out_3), .sel(in_2[0]));  // open: en
endmodule

module ALU (
  input  [31:0] in_1,
  input  [31:0] in_2,
  input  [2:0] in_3,
  output [31:0] out_4
);

  wire [3:0] bit_extender_2_out;
  wire [4:0] bit_extender_1_out;
  wire [15:0] bit_extender_3_out, RotL_out_3, RotR_out_3;
  wire [31:0] and_1_out, ArithR_out_3, bit_extender_4_out, bit_extender_5_out, LogL_out_3, LogR_out_3,
       or_1_out, xor_1_out;

  Bit_Extender #(.in_width(32), .out_width(5)) bit_extender_1 (.in(in_2), .out(bit_extender_1_out));
  Bit_Extender #(.in_width(32), .out_width(4)) bit_extender_2 (.in(in_2), .out(bit_extender_2_out));
  Bit_Extender #(.in_width(32)) bit_extender_3 (.in(in_1), .out(bit_extender_3_out));
  logl LogL (.in_1(in_1), .in_2(bit_extender_1_out), .out_3(LogL_out_3));
  logr LogR (.in_1(in_1), .in_2(bit_extender_1_out), .out_3(LogR_out_3));
  arithr ArithR (.in_1(in_1), .in_2(bit_extender_1_out), .out_3(ArithR_out_3));
  rotl RotL (.in_1(bit_extender_3_out), .in_2(bit_extender_2_out), .out_3(RotL_out_3));
  rotr RotR (.in_1(bit_extender_3_out), .in_2(bit_extender_2_out), .out_3(RotR_out_3));
  assign and_1_out = in_1 & in_2;  // AND_Gate and_1, 32 bits wide
  assign or_1_out = in_1 | in_2;  // OR_Gate or_1, 32 bits wide
  assign xor_1_out = in_1 ^ in_2;  // XOR_Gate xor_1, 32 bits wide
  assign bit_extender_4_out = {{16{1'b0}}, RotL_out_3};  // Bit_Extender bit_extender_4
  assign bit_extender_5_out = {{16{1'b0}}, RotR_out_3};  // Bit_Extender bit_extender_5
  Multiplexer #(.select(3), .width(32)) multiplexer_1 (
    .in0(LogL_out_3), .in1(LogR_out_3), .in2(ArithR_out_3), .in3(bit_extender_4_out),
    .in4(bit_extender_5_out), .in5(and_1_out), .in6(or_1_out), .in7(xor_1_out), .out(out_4), .sel(in_3));  // open: en
endmodule

module logl (
  input  [31:0] in_1,
  input  [4:0] in_2,
  output [31:0] out_3
);

  wire [0:0] bit_extender_5_out;
  wire [1:0] bit_extender_4_out;
  wire [3:0] bit_extender_3_out;
  wire [7:0] bit_extender_2_out;
  wire [15:0] bit_extender_1_out;
  wire [31:0] multiplexer_1_out, multiplexer_2_out, multiplexer_3_out, multiplexer_4_out;

  Bit_Extender #(.in_width(32)) bit_extender_1 (.in({32{1'b0}}), .out(bit_extender_1_out));
  Multiplexer #(.width(32)) multiplexer_1 (
    .in0(in_1), .in1({in_1[15:0], bit_extender_1_out}), .out(multiplexer_1_out), .sel(in_2[4]));  // open: en
  Bit_Extender #(.in_width(32), .out_width(8)) bit_extender_2 (.in({32{1'b0}}), .out(bit_extender_2_out));
  Multiplexer #(.width(32)) multiplexer_2 (
    .in0(multiplexer_1_out), .in1({multiplexer_1_out[23:0], bit_extender_2_out}), .out(multiplexer_2_out),
    .sel(in_2[3]));  // open: en
  Bit_Extender #(.in_width(32), .out_width(4)) bit_extender_3 (.in({32{1'b0}}), .out(bit_extender_3_out));
  Bit_Extender #(.in_width(32), .out_width(2)) bit_extender_4 (.in({32{1'b0}}), .out(bit_extender_4_out));
  Multiplexer #(.width(32)) multiplexer_3 (
    .in0(multiplexer_2_out), .in1({multiplexer_2_out[27:0], bit_extender_3_out}), .out(multiplexer_3_out),
    .sel(in_2[2]));  // open: en
  Bit_Extender #(.in_width(32), .out_width(1)) bit_extender_5 (.in({32{1'b0}}), .out(bit_extender_5_out[0]));
  Multiplexer #(.width(32)) multiplexer_4 (
    .in0(multiplexer_3_out), .in1({multiplexer_3_out[29:0], bit_extender_4_out}), .out(multiplexer_4_out),
    .sel(in_2[1]));  // open: en
  Multiplexer #(.width(32)) multiplexer_5 (
    .in0(multiplexer_4_out), .in1({multiplexer_4_out[30:0], bit_extender_5_out[0]}), .out(out_3),
    .sel(in_2[0]));  // open: en
endmodule

module logr (
  input  [31:0] in_1,
  input  [4:0] in_2,
  output [31:0] out_3
);

  wire [1:0] bit_extender_4_out;
  wire [3:0] bit_extender_3_out;
  wire [7:0] bit_extender_2_out;
  wire [15:0] bit_extender_1_out;
  wire [31:0] multiplexer_1_out, multiplexer_2_out, multiplexer_3_out, multiplexer_4_out;
  wire [31:31] bit_extender_5_out;

  Bit_Extender #(.in_width(32)) bit_extender_1 (.in({32{1'b0}}), .out(bit_extender_1_out));
  Multiplexer #(.width(32)) multiplexer_1 (
    .in0(in_1), .in1({bit_extender_1_out, in_1[31:16]}), .out(multiplexer_1_out), .sel(in_2[4]));  // open: en
  Bit_Extender #(.in_width(32), .out_width(8)) bit_extender_2 (.in({32{1'b0}}), .out(bit_extender_2_out));
  Multiplexer #(.width(32)) multiplexer_2 (
    .in0(multiplexer_1_out), .in1({bit_extender_2_out, multiplexer_1_out[31:8]}), .out(multiplexer_2_out),
    .sel(in_2[3]));  // open: en
  Bit_Extender #(.in_width(32), .out_width(4)) bit_extender_3 (.in({32{1'b0}}), .out(bit_extender_3_out));
  Bit_Extender #(.in_width(32), .out_width(2)) bit_extender_4 (.in({32{1'b0}}), .out(bit_extender_4_out));
  Multiplexer #(.width(32)) multiplexer_3 (
    .in0(multiplexer_2_out), .in1({bit_extender_3_out, multiplexer_2_out[31:4]}), .out(multiplexer_3_out),
    .sel(in_2[2]));  // open: en
  Bit_Extender #(.in_width(32), .out_width(1)) bit_extender_5 (.in({32{1'b0}}), .out(bit_extender_5_out[31]));
  Multiplexer #(.width(32)) multiplexer_4 (
    .in0(multiplexer_3_out), .in1({multiplexer_3_out[31:2], bit_extender_4_out}), .out(multiplexer_4_out),
    .sel(in_2[1]));  // open: en
  Multiplexer #(.width(32)) multiplexer_5 (
    .in0(multiplexer_4_out), .in1({bit_extender_5_out[31], multiplexer_4_out[31:1]}), .out(out_3),
    .sel(in_2[0]));  // open: en
endmodule

module arithr (
  input  [31:0] in_1,
  input  [4:0] in_2,
  output [31:0] out_3
);

  wire [31:31] logr_1_out_3;

  logr logr_1 (.in_1(in_1), .in_2(in_2), .out_3({logr_1_out_3[31], out_3[30:0]}));

  assign out_3[31] = in_1[31];
endmodule
